// Logisim project parity_error_detection.circ as structural Verilog: 3 circuits, main circuit main
module main (
  input  D3,
  input  FLIP_D3,
  input  D2,
  input  FLIP_D2,
  input  D1,
  input  FLIP_D1,
  input  D0,
  input  FLIP_D0,
  input  FLIP_P,
  output P,
  output E
);

  wire R0, R1, R2, R3, RP, xor_1_out, xor_2_out, xor_9_out, xor_10_out, xor_11_out;

  xor xor_1 (xor_1_out, D3, D2);
  xor xor_2 (xor_2_out, D1, D0);
  xor xor_3 (P, xor_1_out, xor_2_out);
  xor xor_4 (R3, D3, FLIP_D3);
  xor xor_5 (R2, D2, FLIP_D2);
  xor xor_6 (R1, D1, FLIP_D1);
  xor xor_7 (R0, D0, FLIP_D0);
  xor xor_8 (RP, P, FLIP_P);
  xor xor_9 (xor_9_out, R3, R2);
  xor xor_10 (xor_10_out, R1, R0);
  xor xor_11 (xor_11_out, xor_9_out, xor_10_out);
  xor xor_12 (E, xor_11_out, RP);

  // Notes on the sheet:
  //   DIGITAL ERROR DETECTION SYSTEM USING PARITY
  //   PARITY GENERATOR (even parity)
  //   P = D3 xor D2 xor D1 xor D0   (3 XOR gates)
  //   Input: 4-bit data D3..D0 (poke the pins)
  //   TRANSMISSION CHANNEL
  //   Set a FLIP switch to 1 to corrupt that bit
  //   PARITY CHECKER
  //   E = R3 xor R2 xor R1 xor R0 xor P
  //   E = 0 : No error     E = 1 : Error detected
endmodule

module parity_generator (
  input  D3,
  input  D2,
  input  D1,
  input  D0,
  output P
);

  wire xor_1_out, xor_2_out;

  xor xor_1 (xor_1_out, D3, D2);
  xor xor_2 (xor_2_out, D1, D0);
  xor xor_3 (P, xor_1_out, xor_2_out);

  // Notes on the sheet:
  //   PARITY GENERATOR (even parity)
  //   P = D3 xor D2 xor D1 xor D0   (3 XOR gates)
endmodule

module parity_checker (
  input  R3,
  input  R2,
  input  R1,
  input  R0,
  input  P,
  output E
);

  wire xor_1_out, xor_2_out, xor_3_out;

  xor xor_1 (xor_1_out, R3, R2);
  xor xor_2 (xor_2_out, R1, R0);
  xor xor_3 (xor_3_out, xor_1_out, xor_2_out);
  xor xor_4 (E, xor_3_out, P);

  // Notes on the sheet:
  //   PARITY CHECKER
  //   E = R3 xor R2 xor R1 xor R0 xor P
  //   E = 0 : No error     E = 1 : Error detected
endmodule
